# Fritzing sketch rbe-robot (saved by Fritzing 0.7.7b)
breadboards: 1

parts:
  IC1 = H-Bridge [package=THT]
  U1 = Arduino Mega
  DC_Power1 = DC Power [voltage=5]
  M1 = DC Motor [part_number=Motor1]
  M2 = DC Motor [part_number=Motor2]
  RE1 = Rotary Encoder [package=THT]
  RE2 = Rotary Encoder [package=THT]

nets:
  N1: IC1.1_2EN, U1.D8
  N2: IC1.1A, U1.D33
  N3: IC1.1Y, M1.pin_2
  GND1: IC1.GND1, IC1.GND3, IC1.GND4, U1.GND
  GND2: IC1.GND2, DC_Power1.GND
  N4: IC1.2Y, M1.pin_1
  N5: IC1.2A, U1.D34
  N6: IC1.VCC2, DC_Power1.V+
  N7: IC1.3_4EN, U1.D9
  N8: IC1.3A, U1.D36
  N9: IC1.3Y, M2.pin_1
  N10: IC1.4Y, M2.pin_2
  N11: IC1.4A, U1.D35
  N12: IC1.VCC1, U1.+5V, RE1.EncoderPinA, RE2.EncoderPinA
  N13: U1.D19, RE2.EncoderPinC
  N14: U1.D20, RE1.EncoderPinC
